# Fritzing sketch LarsAliDrone-Fritzing (saved by Fritzing 0.8.7b)
breadboards: 2

parts:
  M1 = DOIT Esp32 DevKit v1 (30 pins long, 11 pins width) [part_number=ESP32S-PIN30]
  U1 = POT [package=pot_mammoth]
  Part1 = Thumb Joystick
  S1 = Pushbutton [package="[THT]"]
  R1 = Resistor [tolerance=±5% resistance=220 package=THT]
  S2 = Pushbutton [package="[THT]"]
  R2 = Resistor [tolerance=±5% resistance=220 package=THT]

nets:
  3V3: M1.3V3, U1.E, Part1.VCC, R1.Pin_1, R2.Pin_1
  GND: M1.GND, U1.S, Part1.GND, S2.Pin_1, S2.Pin_2
  N1: M1.D15, S2.Pin_3, S2.Pin_4, R2.Pin_0
  N2: M1.D23, S1.Pin_3, S1.Pin_4, R1.Pin_0
  N3: M1.D34, Part1.VERT
  N4: M1.D35, Part1.HORZ
  N5: M1.D32, Part1.SEL
  N6: M1.D33, U1.A
  N7: S1.Pin_1, S1.Pin_2

custom parts:
  DOIT Esp32 DevKit v1 (30 pins long, 11 pins width): The DOIT Esp32 DevKit v1 is one of the development board created by DOIT to evaluate the ESP-WROOM-32 module. It is based on the ESP32 microcontroller that boasts Wifi, Bluetooth, Ethernet and Low Power support all in a single chip. (vanepp) made breadboard work, adjusted pin numbering and labels and reduced size of schematic and cleaned up pcb. This chip is 30pins long (2 x15) and 11 pins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
